// Logisim project rd53.circ as structural Verilog: 1 circuit, main circuit main
module main (
  input  v0,
  input  v1,
  input  v2,
  input  v3,
  input  v4,
  output v5_2,
  output v5_1,
  output v5_0
);

  wire and_1_out, nand_1_out, nand_2_out, nand_3_out, nand_4_out, nand_5_out, nand_6_out, nand_7_out,
       nand_8_out, nand_9_out, nand_10_out, nand_11_out, nand_12_out, nand_13_out, nand_15_out, nand_16_out,
       nor_1_out, nor_2_out, nor_3_out, nor_4_out, nor_5_out, nor_6_out, nor_7_out, nor_8_out, nor_9_out,
       nor_10_out, not_1_out, not_2_out, not_3_out, not_4_out, not_5_out, not_6_out, not_7_out, not_8_out;

  not not_1 (not_1_out, v0);
  not not_2 (not_2_out, v2);
  not not_3 (not_3_out, v1);
  nor nor_1 (nor_1_out, v3, v4);
  nand nand_1 (nand_1_out, not_1_out, not_2_out);
  nand nand_2 (nand_2_out, v0, v2);
  and and_1 (and_1_out, v0, v2, v2);
  not not_4 (not_4_out, nor_1_out);
  nand nand_3 (nand_3_out, nand_1_out, v1);
  nand nand_4 (nand_4_out, v0, v1);
  nand nand_5 (nand_5_out, v1, not_4_out);
  nand nand_6 (nand_6_out, nand_3_out, not_3_out);
  nor nor_2 (nor_2_out, v0, v2);
  nand nand_7 (nand_7_out, nand_2_out, nand_5_out);
  nand nand_8 (nand_8_out, v3, v4);
  nand nand_9 (nand_9_out, nand_3_out, and_1_out);
  nand nand_10 (nand_10_out, nand_6_out, nand_4_out);
  not not_5 (not_5_out, nand_8_out);
  nor nor_3 (nor_3_out, nand_10_out, v2);
  nand nand_11 (nand_11_out, nand_10_out, v2);
  nor nor_4 (nor_4_out, not_1_out, not_2_out);
  not not_6 (not_6_out, nor_3_out);
  nor nor_5 (nor_5_out, not_5_out, nor_1_out);
  nor nor_6 (nor_6_out, nor_2_out, nor_1_out);
  nand nand_12 (nand_12_out, nand_9_out, not_5_out);
  not not_7 (not_7_out, nor_5_out);
  nor nor_7 (nor_7_out, nor_4_out, nor_6_out);
  nand nand_13 (nand_13_out, not_6_out, nand_11_out);
  nand nand_14 (v5_0, nand_7_out, nand_12_out);
  not not_8 (not_8_out, nand_13_out);
  nand nand_15 (nand_15_out, nand_13_out, not_7_out);
  nand nand_16 (nand_16_out, not_8_out, nor_5_out);
  nand nand_17 (v5_1, nand_15_out, nand_16_out);
  nor nor_8 (nor_8_out, not_3_out, v5_1);
  nor nor_9 (nor_9_out, not_5_out, nor_8_out);
  nor nor_10 (nor_10_out, nor_7_out, nor_9_out);
  nor nor_11 (v5_2, nor_10_out, v5_0);

  // Notes on the sheet:
  //   w1019
  //   w1022
  //   w1020
  //   w1083
  //   x0
  //   w1121
  //   w1079
  //   w922
  //   w1119
  //   w1113
  //   x1
  //   w1111
  //   w1115
  //   w1026
  //   w923
  //   w1090
  //   w1027
  //   w1088
  //   w953
  //   w1109
  //   w945
  //   w949
  //   w947
  //   w1107
  //   w1117
  //   w1029
  //   w1028
  //   x2
  //   w1077
  //   w1105
  //   w1103
  //   w948
  //   x3
  //   w946
endmodule
