// Logisim project subrd53.circ as structural Verilog: 1 circuit, main circuit main
module main (
);

  wire nand_1_out, nand_2_out, nand_3_out, nand_4_out, not_1_out, undriven, undriven_2, undriven_3,
       undriven_4, undriven_5;

  nand nand_1 (nand_1_out, undriven, undriven_2);
  nand nand_2 (nand_2_out, undriven_3, undriven_4);
  not not_1 (not_1_out, nand_1_out);
  nand nand_3 (nand_3_out, nand_2_out, undriven_5);
  nand nand_4 (nand_4_out, not_1_out, nand_3_out);

  // Notes on the sheet:
  //   v4
  //   v3
  //   v2
  //   v0
  //   w1119
  //   w1026
  //   w1121
  //   w1088
  //   w1090
  //   w1117
endmodule
