// Logisim project rd73.circ as structural Verilog: 1 circuit, main circuit main
module main (
  input  v0,
  input  v1,
  input  v2,
  input  v3,
  input  v4,
  input  v5,
  input  v6,
  output v7_2,
  output v7_0,
  output v7_1
);

  wire nand_1_out, nand_2_out, nand_3_out, nand_4_out, nand_5_out, nand_6_out, nand_7_out, nand_8_out,
       nand_9_out, nand_10_out, nand_11_out, nand_12_out, nand_13_out, nand_14_out, nand_15_out, nand_16_out,
       nand_17_out, nand_18_out, nand_19_out, nand_20_out, nand_21_out, nand_22_out, nand_23_out,
       nand_24_out, nand_25_out, nand_26_out, nand_27_out, nand_28_out, nand_29_out, nand_30_out,
       nand_31_out, nand_32_out, nand_33_out, nand_34_out, nand_36_out, nand_37_out, nand_38_out, nor_1_out,
       nor_2_out, nor_3_out, nor_4_out, nor_5_out, nor_6_out, nor_7_out, nor_8_out, nor_9_out, nor_10_out,
       nor_11_out, nor_12_out, nor_13_out, nor_14_out, nor_15_out, nor_16_out, nor_17_out, nor_18_out,
       not_1_out, not_2_out, not_3_out, not_4_out, not_5_out, not_6_out, not_7_out, not_8_out, not_9_out,
       not_10_out, not_11_out, not_12_out, not_13_out, not_14_out, not_15_out, not_16_out, not_17_out,
       not_19_out, not_20_out, not_21_out, not_22_out, not_23_out, not_25_out, not_26_out;

  not not_1 (not_1_out, v0);
  not not_2 (not_2_out, v1);
  not not_3 (not_3_out, v2);
  not not_4 (not_4_out, v2);
  not not_5 (not_5_out, v3);
  not not_6 (not_6_out, v4);
  not not_7 (not_7_out, not_2_out);
  not not_8 (not_8_out, not_2_out);
  not not_9 (not_9_out, v1);
  nor nor_1 (nor_1_out, v5, v6);
  nor nor_2 (nor_2_out, v5, v6);
  not not_10 (not_10_out, not_1_out);
  not not_11 (not_11_out, not_4_out);
  not not_12 (not_12_out, nor_1_out);
  not not_13 (not_13_out, nor_2_out);
  not not_14 (not_14_out, not_10_out);
  nand nand_1 (nand_1_out, not_1_out, not_9_out);
  nand nand_2 (nand_2_out, not_8_out, v3);
  nor nor_3 (nor_3_out, not_8_out, v3);
  nand nand_3 (nand_3_out, not_3_out, nor_1_out);
  not not_15 (not_15_out, nor_3_out);
  nand nand_4 (nand_4_out, v4, nand_3_out);
  nand nand_5 (nand_5_out, v4, nand_3_out);
  nand nand_6 (nand_6_out, not_12_out, nor_2_out);
  nand nand_7 (nand_7_out, not_10_out, not_7_out);
  nand nand_8 (nand_8_out, nand_5_out, nand_5_out);
  not not_16 (not_16_out, nand_6_out);
  nand nand_9 (nand_9_out, nand_7_out, nand_1_out);
  nand nand_10 (nand_10_out, not_15_out, v4, v4);
  not not_17 (not_17_out, nand_9_out);
  nand nand_11 (nand_11_out, nand_2_out, nand_10_out);
  nor nor_4 (nor_4_out, not_3_out, nor_1_out);
  nand nand_12 (nand_12_out, nand_9_out, v2);
  not not_18 (nand_6_out, nand_11_out);
  nand nand_13 (nand_13_out, not_3_out, not_17_out);
  nor nor_5 (nor_5_out, nor_4_out, not_13_out);
  nand nand_14 (nand_14_out, nand_4_out, nand_4_out);
  nand nand_15 (nand_15_out, not_11_out, not_13_out);
  nand nand_16 (nand_16_out, nand_13_out, nand_12_out);
  not not_19 (not_19_out, nor_5_out);
  nand nand_17 (nand_17_out, nand_15_out, nand_15_out);
  not not_20 (not_20_out, nand_16_out);
  nand nand_18 (nand_18_out, nand_16_out, v3);
  nand nand_19 (nand_19_out, not_5_out, not_20_out);
  nand nand_20 (nand_20_out, nand_6_out, not_6_out);
  nand nand_21 (nand_21_out, nand_20_out, nand_3_out);
  not not_21 (not_21_out, nand_2_out);
  nor nor_6 (nor_6_out, nand_6_out, not_19_out);
  nand nand_22 (nand_22_out, nand_20_out, nand_17_out);
  nand nand_23 (nand_23_out, nand_19_out, nand_18_out);
  nand nand_24 (nand_24_out, not_21_out, nand_8_out);
  not not_22 (not_22_out, nand_23_out);
  nand nand_25 (nand_25_out, nand_23_out, v4);
  nand nand_26 (nand_26_out, nand_24_out, nand_22_out);
  nand nand_27 (nand_27_out, not_22_out, not_6_out);
  nor nor_7 (nor_7_out, nand_26_out, nor_6_out);
  nand nand_28 (nand_28_out, nand_27_out, nand_25_out);
  not not_23 (not_23_out, nand_28_out);
  nor nor_8 (nor_8_out, nor_7_out, nor_7_out);
  nand nand_29 (nand_29_out, nand_28_out, nand_6_out);
  nand nand_30 (nand_30_out, not_23_out, not_16_out);
  nand nand_31 (nand_31_out, nand_30_out, nand_29_out);
  not not_24 (v7_1, nand_31_out);
  not not_25 (not_25_out, not_14_out);
  nor nor_9 (nor_9_out, not_14_out, nand_31_out);
  nor nor_10 (nor_10_out, nor_9_out, not_19_out);
  nand nand_32 (nand_32_out, v7_1, nand_14_out);
  nand nand_33 (nand_33_out, not_25_out, not_11_out);
  not not_26 (not_26_out, nor_9_out);
  nor nor_11 (nor_11_out, nand_33_out, nor_2_out);
  nor nor_12 (nor_12_out, nor_5_out, not_26_out);
  nand nand_34 (nand_34_out, nor_10_out, nand_21_out);
  nor nor_13 (nor_13_out, nand_32_out, nand_2_out);
  nand nand_35 (v7_2, nor_12_out, nor_8_out);
  nand nand_36 (nand_36_out, nand_34_out, nand_34_out);
  nor nor_14 (nor_14_out, nor_13_out, nor_13_out);
  nor nor_15 (nor_15_out, nor_11_out, nor_11_out);
  nand nand_37 (nand_37_out, nand_36_out, nand_6_out);
  nor nor_16 (nor_16_out, nor_15_out, nand_6_out);
  nor nor_17 (nor_17_out, nor_10_out, nor_14_out);
  nand nand_38 (nand_38_out, v7_2, nand_37_out);
  nor nor_18 (nor_18_out, nor_17_out, nor_16_out);
  nand nand_39 (v7_0, nand_38_out, nor_18_out);

  // Notes on the sheet:
  //   w10408
  //   w10414
  //   w10412
  //   w10400
  //   w10409
  //   w10407
  //   w10415
  //   w10416
  //   w9684
  //   w9853
  //   w10401
  //   w10410
  //   w10413
  //   w10419
  //   w10402
  //   w10018
  //   w9952
  //   w10418
  //   w9846
  //   w9685
  //   w10405
  //   x6
  //   x2
  //   w9863
  //   w10020
  //   w10417
  //   w9859
  //   w9998
  //   x3
  //   w10399
  //   w9865
  //   w9729
  //   w10016
  //   w10404
  //   w10014
  //   w9687
  //   x4
  //   w9860
  //   w10411
  //   x7
  //   x5
  //   w10398
  //   w10012
  //   w9956
  //   w10010
  //   w9988
  //   w10406
  //   w9726
  //   w9992
  //   w9861
  //   w9990
  //   w10397
  //   w10008
  //   w9856
  //   w10006
  //   x8
  //   w9862
  //   x9
  //   w10396
  //   w10004
  //   w10002
  //   w9743
  //   w10403
  //   w9695
  //   w10394
  //   w9693
  //   w9870
  //   w9872
  //   w10393
  //   x12
  //   w9725
  //   x0
  //   x10
  //   w9680
  //   x1
  //   x13
  //   w9977
  //   x11
  //   x9718
  //   w9717
  //   w9986
  //   w9747
endmodule
